// Logisim project ALU - Copy.circ as structural Verilog: 1 circuit, main circuit Full-ALU
module Full_ALU (
  input  s2,
  input  s1,
  input  s0,
  input  A3,
  input  A2,
  input  A1,
  input  A0,
  input  B3,
  input  B2,
  input  B1,
  input  B0,
  output CF,
  output OF,
  output ZF,
  output SF,
  output C,
  output _3,
  output _2,
  output _1,
  output _0,
  output C_out,
  output out_22,
  output F1,
  output F2,
  output out_25
);

  wire n7400_1__3__1y, n7400_1__6__2y, n7400_1__8__3y, n7400_1__11__4y, n7408_1__11__4y, n7408_2__3__1y,
       n7408_2__6__2y, n7408_2__8__3y, n7408_2__11__4y, n7408_3__3__1y, n7408_3__6__2y, n7408_3__8__3y,
       n7408_3__11__4y, n7432_1__3__1y, n7432_1__8__3y, n7432_1__11__4y, n7432_2__3__1y, n7432_2__6__2y,
       n7432_2__8__3y, n7432_2__11__4y, n7432_3__3__1y, n7432_3__6__2y, n7432_3__8__3y, n7432_3__11__4y,
       n7483_1__6__s2, n7483_1__14__cout, n7483_2__6__s2, n7486_1__3__1y, n7486_1__8__3y, n7486_1__11__4y,
       n7486_2__3__1y, n7486_2__6__2y, n7486_2__8__3y, n7486_2__11__4y;

  _7400 u_7400_1 (
    ._1__1A(s0), ._2__1B(B0), ._3__1Y(n7400_1__3__1y), ._4__2A(s0), ._5__2B(B1), ._6__2Y(n7400_1__6__2y),
    ._13__4B(s0), ._12__4A(B2), ._11__4Y(n7400_1__11__4y), ._10__3B(s0), ._9__3A(B3), ._8__3Y(n7400_1__8__3y));  // open: _7__GND, _14__Vcc
  _7432 u_7432_1 (
    ._1__1A(n7432_1__11__4y), ._2__1B(n7432_1__8__3y), ._3__1Y(n7432_1__3__1y), ._13__4B(_0), ._12__4A(_1),
    ._11__4Y(n7432_1__11__4y), ._10__3B(_2), ._9__3A(_3), ._8__3Y(n7432_1__8__3y));  // open: _4__2A, _5__2B, _6__2Y, _7__GND, _14__Vcc
  _7486 u_7486_1 (
    ._1__1A(1'b1), ._2__1B(s1), ._3__1Y(n7486_1__3__1y), ._4__2A(1'b1), ._5__2B(n7432_1__3__1y), ._6__2Y(ZF),
    ._13__4B(1'b1), ._12__4A(s0), ._11__4Y(n7486_1__11__4y), ._10__3B(C), ._9__3A(n7483_2__6__s2),
    ._8__3Y(n7486_1__8__3y));  // open: _7__GND, _14__Vcc
  _7483 u_7483_1 (
    ._1__A4(n7432_3__6__2y), ._3__A3(n7432_2__8__3y), ._4__B3(n7432_2__8__3y), ._6__S2(n7483_1__6__s2),
    ._7__B2(1'b0), ._8__A2(1'b0), ._16__B4(n7400_1__6__2y), ._15__S4(_1), ._14__Cout(n7483_1__14__cout),
    ._13__Cin(n7432_2__11__4y), ._11__B1(n7400_1__3__1y), ._10__A1(n7432_3__3__1y), ._9__S1(_0));  // open: _2__S3, _5__Vcc, _12__GND
  _7408 u_7408_1 (
    ._1__1A(C), ._2__1B(n7486_1__3__1y), ._3__1Y(CF), ._4__2A(n7486_1__3__1y), ._5__2B(n7486_1__8__3y),
    ._6__2Y(OF), ._14__Vcc(n7486_1__11__4y), ._13__4B(n7486_1__11__4y), ._12__4A(s1),
    ._11__4Y(n7408_1__11__4y));  // open: _7__GND, _10__3B, _9__3A, _8__3Y
  _7432 u_7432_2 (
    ._1__1A(n7408_1__11__4y), ._2__1B(n7408_2__11__4y), ._3__1Y(n7432_2__3__1y), ._4__2A(n7408_1__11__4y),
    ._5__2B(n7408_2__8__3y), ._6__2Y(n7432_2__6__2y), ._13__4B(n7408_1__11__4y), ._12__4A(n7408_2__3__1y),
    ._11__4Y(n7432_2__11__4y), ._10__3B(n7408_1__11__4y), ._9__3A(n7408_2__6__2y), ._8__3Y(n7432_2__8__3y));  // open: _7__GND, _14__Vcc
  _7483 u_7483_2 (
    ._1__A4(n7432_3__8__3y), ._3__A3(n7432_2__3__1y), ._4__B3(n7432_2__3__1y), ._6__S2(n7483_2__6__s2),
    ._7__B2(1'b0), ._8__A2(1'b0), ._16__B4(n7400_1__8__3y), ._15__S4(_3), ._14__Cout(C),
    ._13__Cin(n7432_2__6__2y), ._11__B1(n7432_3__11__4y), ._10__A1(n7400_1__11__4y), ._9__S1(_2));  // open: _2__S3, _5__Vcc, _12__GND
  _7408 u_7408_2 (
    ._1__1A(n7486_1__3__1y), ._2__1B(s2), ._3__1Y(n7408_2__3__1y), ._4__2A(n7486_1__3__1y),
    ._5__2B(n7483_1__6__s2), ._6__2Y(n7408_2__6__2y), ._13__4B(n7486_1__3__1y), ._12__4A(n7483_2__6__s2),
    ._11__4Y(n7408_2__11__4y), ._10__3B(n7486_1__3__1y), ._9__3A(n7483_1__14__cout), ._8__3Y(n7408_2__8__3y));  // open: _7__GND, _14__Vcc
  _7432 u_7432_3 (
    ._1__1A(A0), ._2__1B(n7408_3__11__4y), ._3__1Y(n7432_3__3__1y), ._4__2A(A1), ._5__2B(n7408_3__8__3y),
    ._6__2Y(n7432_3__6__2y), ._13__4B(A2), ._12__4A(n7408_3__3__1y), ._11__4Y(n7432_3__11__4y), ._10__3B(A3),
    ._9__3A(n7408_3__6__2y), ._8__3Y(n7432_3__8__3y));  // open: _7__GND, _14__Vcc
  _7408 u_7408_3 (
    ._1__1A(s1), ._2__1B(n7486_2__11__4y), ._3__1Y(n7408_3__3__1y), ._4__2A(s1), ._5__2B(n7486_2__8__3y),
    ._6__2Y(n7408_3__6__2y), ._13__4B(s1), ._12__4A(n7486_2__3__1y), ._11__4Y(n7408_3__11__4y), ._10__3B(s1),
    ._9__3A(n7486_2__6__2y), ._8__3Y(n7408_3__8__3y));  // open: _7__GND, _14__Vcc
  _7486 u_7486_2 (
    ._1__1A(s0), ._2__1B(B0), ._3__1Y(n7486_2__3__1y), ._4__2A(s0), ._5__2B(B1), ._6__2Y(n7486_2__6__2y),
    ._13__4B(s0), ._12__4A(B2), ._11__4Y(n7486_2__11__4y), ._10__3B(s0), ._9__3A(B3), ._8__3Y(n7486_2__8__3y));  // open: _7__GND, _14__Vcc

  assign C_out = C;
  assign F1 = _1;
  assign F2 = _2;
  assign out_22 = _0;
  assign out_25 = _3;
  assign SF = _3;

  // Notes on the sheet:
  //   F3
  //   F0
  //   C in
  //   X0
  //   Y0
  //   Z1
  //   X1
  //   Y1
  //   Z2
  //   X2
  //   Y2
  //   Z3
  //   X3
  //   Y3
  //   C1
  //   C2
  //   C3
  //   s1s0'
endmodule
